# Fritzing sketch Wiring (saved by Fritzing 0.9.6b)

parts:
  Componente1 = Arduino Uno (Rev3)  # not connected
  RelayShield1 = SeeedStudio - Relay Shield v3.0
  Componente2 = Adafruit PN532 NFC RFID Controller Shield [part_number="Adafruit #789"]  # not connected
  6_pin_connector_female_1 = Camdenboss CTB0158-6 [part_number=CTB0158-6 package=THT]
  6_pin_connector_female_2 = Camdenboss CTB0158-6 [part_number=CTB0158-6 package=THT]
  Digital_Outputs_rack_2 = Camdenboss CTB0158-8 [part_number=CTB0158-8 package=THT]  # not connected
  Digital_Outputs_rack_1 = Camdenboss CTB0158-8 [part_number=CTB0158-8 package=THT]  # not connected
  Digital_Inputs_rack_1 = Camdenboss CTB0158-8 [part_number=CTB0158-8 package=THT]
  Digital_Inputs_rack_2 = Camdenboss CTB0158-8 [part_number=CTB0158-8 package=THT]  # not connected
  Configurable_Outputs_rack_1 = Camdenboss CTB0158-8 [part_number=CTB0158-8 package=THT]  # not connected
  Configurable_Inputs_rack_1 = Camdenboss CTB0158-8 [part_number=CTB0158-8 package=THT]  # not connected
  Configurable_Inputs_rack_2 = Camdenboss CTB0158-8 [part_number=CTB0158-8 package=THT]  # not connected
  Configurable_Outputs_rack_2 = Camdenboss CTB0158-8 [part_number=CTB0158-8 package=THT]  # not connected
  Remote = Camdenboss CTB0158-4 [part_number=CTB0158-4 package=THT]  # not connected
  Power = Camdenboss CTB0158-4 [part_number=CTB0158-4 package=THT]
  Safety_Emergency_Stop = Camdenboss CTB0158-4 [part_number=CTB0158-4 package=THT]  # not connected
  Safety_Safeguard_Stop = Camdenboss CTB0158-4 [part_number=CTB0158-4 package=THT]  # not connected
  Analog_Inputs = Camdenboss CTB0158-4 [part_number=CTB0158-4 package=THT]  # not connected
  Analog_Outputs = Camdenboss CTB0158-4 [part_number=CTB0158-4 package=THT]  # not connected
  J1 = Camdenboss CTB0158-2 [part_number=CTB0158-2 package=THT]
  JACK_(male) = 2.1mm Barrel Jack with Terminal Block
  IC1 = Voltage Regulator [package=to220-igo]

nets:
  N1: RelayShield1.NC1, 6_pin_connector_female_1.pin4
  N2: RelayShield1.COM1, 6_pin_connector_female_1.pin5
  N3: RelayShield1.NO1, 6_pin_connector_female_1.pin6
  N4: RelayShield1.NC2, 6_pin_connector_female_1.pin1
  N5: RelayShield1.COM2, 6_pin_connector_female_1.pin2
  N6: RelayShield1.NO2, 6_pin_connector_female_1.pin3
  N7: RelayShield1.NC3, 6_pin_connector_female_2.pin4
  N8: RelayShield1.COM3, 6_pin_connector_female_2.pin5
  N9: RelayShield1.NO3, 6_pin_connector_female_2.pin6
  N10: RelayShield1.NC4, 6_pin_connector_female_2.pin1
  N11: RelayShield1.COM4, 6_pin_connector_female_2.pin2
  N12: RelayShield1.NO4, 6_pin_connector_female_2.pin3
  N13: 6_pin_connector_female_1.terminal_2, Digital_Inputs_rack_1.terminal_6
  N14: 6_pin_connector_female_1.terminal_3, Digital_Inputs_rack_1.terminal_5
  N15: 6_pin_connector_female_1.terminal_5, Digital_Inputs_rack_1.terminal_8
  N16: 6_pin_connector_female_1.terminal_6, Digital_Inputs_rack_1.terminal_7
  N17: Power.terminal_2, J1.terminal_2
  N18: Power.terminal_3, J1.terminal_1
  N19: J1.pin1, JACK_(male).NEG, IC1.GND
  N20: J1.pin2, IC1.IN
  N21: JACK_(male).POS, IC1.OUT

notes:
  Analog
  Analog Outputs | Analog Inputs
  Digital Outputs
  Digital Inputs
  Configurable Outputs
  Configurable Inputs
  Power
  Remote
  Safety
  Safeguard Stop | Emergency
  Arduino UNO rev3
  Seed Studio Relay Shield v3
  Adafruit PNF532 Shield v1
  6-pin circular connector
  24V
  DI0
  DI1
  GND
  9V voltage regulator
  power jack 5.5x2.1 mm

custom parts:
  SeeedStudio - Relay Shield v3.0: Description TheRelay Shield provides four high quality relay that can control high current loads to Arduino / Seeeduino boards. It also provides NO (Normally Open) / NC (Normally Closed) interface. It could be a nice solution for controlling devices that could not be directly controlled by Arduino's Digital I/Os. Standardized shield form factor enables smooth connection with Arduino and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
  Adafruit PN532 NFC RFID Controller Shield: We've taken our popular Adafruit PN532 breakout board and turned it into a shield - the perfect tool for any 13.56MHz RFID or NFC application. The Adafruit NFC shield uses the PN532 chip-set (the most popular NFC chip on the market) and is what is embedded in pretty much every phone or device that does NFC. This chipset is very powerful, and can pretty much do it all, such as read and write to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
